# Fritzing sketch Fritzing Sketch (saved by Fritzing 0.9.3b)
breadboards: 1

parts:
  Part1 = Bluetooth HC-05 Macho
  R2 = Resistor [tolerance=±5% resistance=220 package=THT]
  Part2 = Arduino Uno (Rev3)
  R3 = Resistor [tolerance=±5% resistance=220 package=THT]

nets:
  N1: Part1.State, Part2.5V
  N2: Part1.TXD, Part2.D2
  N3: Part1.RXD, R2.Pin_1, R3.Pin_1
  GND: Part1.GND, Part2.GND, R3.Pin_0
  N4: R2.Pin_0, Part2.D3_PWM
